# Fritzing sketch ibutton_reader (saved by Fritzing 0.8.5b)
circuit board: 7cm x 5cm
breadboards: 1

parts:
  WeMos_D1_Mini2 = WeMos D1 Mini
  iButton_Reader_connector = Header 4 [part_number="(data, led-, led+, GND)" package=molex-1x4_lock]
  R1 = Resistor [tolerance=±10% resistance=4.7k package=THT]
  Factory_reset = Pushbutton [package="[THT]"]
  R2 = Resistor [tolerance=±5% resistance=220 package=THT]
  230V = Screw terminal - 2 pins [package=THT]  # not connected

nets:
  N1: WeMos_D1_Mini2.3V3, R1.Pin_0
  N2: WeMos_D1_Mini2.D1, iButton_Reader_connector.1, R1.Pin_1
  N3: WeMos_D1_Mini2.D2, R2.Pin_0
  N4: WeMos_D1_Mini2.D3, Factory_reset.Pin_3, Factory_reset.Pin_4
  N5: WeMos_D1_Mini2.G, iButton_Reader_connector.2, iButton_Reader_connector.4, Factory_reset.Pin_1, Factory_reset.Pin_2
  N6: iButton_Reader_connector.3, R2.Pin_1
